# Fritzing sketch Simple Color Sensor Wiring (saved by Fritzing 0.7.12b)
breadboards: 1

parts:
  Arduino1 = Arduino
  R1 = Photocell (LDR) [package=THT]
  LED1 = RGB LED (com. anode, rbg) [package="5 mm [THT]"]
  R2 = Resistor [tolerance=±5% resistance=1k package=THT]
  R4 = Resistor [tolerance=±5% resistance=200 package=THT]
  R5 = Resistor [tolerance=±5% resistance=200 package=THT]
  R6 = Resistor [tolerance=±5% resistance=200 package=THT]

nets:
  N1: Arduino1.D11, R6.Pin_1
  N2: Arduino1.D10, R4.Pin_1
  N3: Arduino1.D9, R5.Pin_1
  N4: Arduino1.+5V, R1.pin_1
  N5: Arduino1.GND, LED1.common_anode, R2.Pin_0
  N6: Arduino1.A0, R1.pin_0, R2.Pin_1
  N7: LED1.red_cathode, R5.Pin_0
  N8: LED1.blue_cathode, R4.Pin_0
  N9: LED1.green_cathode, R6.Pin_0
